// Logisim project GPR.circ as structural Verilog: 3 circuits, main circuit GPR
module GPR (
  input  clk,
  input  [31:0] wdata,
  input  [4:0] CH,
  input  EN,
  input  [4:0] RDS1,
  input  [4:0] RDS2,
  output [31:0] RD1,
  output [31:0] RD2
);

  wire decoder_1_out1, decoder_1_out2, decoder_1_out3, decoder_1_out4, decoder_1_out5, decoder_1_out6,
       decoder_1_out7, decoder_1_out8, decoder_1_out9, decoder_1_out10, decoder_1_out11, decoder_1_out12,
       decoder_1_out13, decoder_1_out14, decoder_1_out15, decoder_1_out16, decoder_1_out17, decoder_1_out18,
       decoder_1_out19, decoder_1_out20, decoder_1_out21, decoder_1_out22, decoder_1_out23, decoder_1_out24,
       decoder_1_out25, decoder_1_out26, decoder_1_out27, decoder_1_out28, decoder_1_out29, decoder_1_out30,
       decoder_1_out31;
  wire [31:0] register_1_q, register_3_q, register_4_q, register_5_q, register_6_q, register_7_q,
       register_8_q, register_9_q, register_10_q, register_11_q, register_12_q, register_13_q, register_14_q,
       register_15_q, register_16_q, register_17_q, register_18_q, register_19_q, register_20_q,
       register_21_q, register_22_q, register_23_q, register_24_q, register_25_q, register_26_q,
       register_27_q, register_28_q, register_29_q, register_30_q, register_31_q, register_32_q;

  Decoder #(.select(5)) decoder_1 (
    .out1(decoder_1_out1), .out2(decoder_1_out2), .out3(decoder_1_out3), .out4(decoder_1_out4),
    .out5(decoder_1_out5), .out6(decoder_1_out6), .out7(decoder_1_out7), .out8(decoder_1_out8),
    .out9(decoder_1_out9), .out10(decoder_1_out10), .out11(decoder_1_out11), .out12(decoder_1_out12),
    .out13(decoder_1_out13), .out14(decoder_1_out14), .out15(decoder_1_out15), .out16(decoder_1_out16),
    .out17(decoder_1_out17), .out18(decoder_1_out18), .out19(decoder_1_out19), .out20(decoder_1_out20),
    .out21(decoder_1_out21), .out22(decoder_1_out22), .out23(decoder_1_out23), .out24(decoder_1_out24),
    .out25(decoder_1_out25), .out26(decoder_1_out26), .out27(decoder_1_out27), .out28(decoder_1_out28),
    .out29(decoder_1_out29), .out30(decoder_1_out30), .out31(decoder_1_out31), .sel(CH), .en(EN));  // open: out0
  Register #(.width(32)) register_1 (.D(wdata), .en(decoder_1_out24), .clk(clk), .Q(register_1_q));  // open: clr
  Register #(.width(32)) register_2 (.D(wdata), .en(1'b0), .clk(clk));  // open: Q, clr
  Register #(.width(32)) register_3 (.D(wdata), .en(decoder_1_out8), .clk(clk), .Q(register_3_q));  // open: clr
  Register #(.width(32)) register_4 (.D(wdata), .en(decoder_1_out25), .clk(clk), .Q(register_4_q));  // open: clr
  Register #(.width(32)) register_5 (.D(wdata), .en(decoder_1_out1), .clk(clk), .Q(register_5_q));  // open: clr
  Register #(.width(32)) register_6 (.D(wdata), .en(decoder_1_out9), .clk(clk), .Q(register_6_q));  // open: clr
  Register #(.width(32)) register_7 (.D(wdata), .en(decoder_1_out16), .clk(clk), .Q(register_7_q));  // open: clr
  Register #(.width(32)) register_8 (.D(wdata), .en(decoder_1_out26), .clk(clk), .Q(register_8_q));  // open: clr
  Register #(.width(32)) register_9 (.D(wdata), .en(decoder_1_out2), .clk(clk), .Q(register_9_q));  // open: clr
  Register #(.width(32)) register_10 (.D(wdata), .en(decoder_1_out10), .clk(clk), .Q(register_10_q));  // open: clr
  Register #(.width(32)) register_11 (.D(wdata), .en(decoder_1_out17), .clk(clk), .Q(register_11_q));  // open: clr
  Register #(.width(32)) register_12 (.D(wdata), .en(decoder_1_out27), .clk(clk), .Q(register_12_q));  // open: clr
  Register #(.width(32)) register_13 (.D(wdata), .en(decoder_1_out3), .clk(clk), .Q(register_13_q));  // open: clr
  Register #(.width(32)) register_14 (.D(wdata), .en(decoder_1_out11), .clk(clk), .Q(register_14_q));  // open: clr
  Register #(.width(32)) register_15 (.D(wdata), .en(decoder_1_out18), .clk(clk), .Q(register_15_q));  // open: clr
  Register #(.width(32)) register_16 (.D(wdata), .en(decoder_1_out28), .clk(clk), .Q(register_16_q));  // open: clr
  Register #(.width(32)) register_17 (.D(wdata), .en(decoder_1_out4), .clk(clk), .Q(register_17_q));  // open: clr
  Register #(.width(32)) register_18 (.D(wdata), .en(decoder_1_out12), .clk(clk), .Q(register_18_q));  // open: clr
  Register #(.width(32)) register_19 (.D(wdata), .en(decoder_1_out19), .clk(clk), .Q(register_19_q));  // open: clr
  Register #(.width(32)) register_20 (.D(wdata), .en(decoder_1_out29), .clk(clk), .Q(register_20_q));  // open: clr
  Register #(.width(32)) register_21 (.D(wdata), .en(decoder_1_out5), .clk(clk), .Q(register_21_q));  // open: clr
  Register #(.width(32)) register_22 (.D(wdata), .en(decoder_1_out13), .clk(clk), .Q(register_22_q));  // open: clr
  Register #(.width(32)) register_23 (.D(wdata), .en(decoder_1_out20), .clk(clk), .Q(register_23_q));  // open: clr
  Register #(.width(32)) register_24 (.D(wdata), .en(decoder_1_out30), .clk(clk), .Q(register_24_q));  // open: clr
  Register #(.width(32)) register_25 (.D(wdata), .en(decoder_1_out6), .clk(clk), .Q(register_25_q));  // open: clr
  Register #(.width(32)) register_26 (.D(wdata), .en(decoder_1_out14), .clk(clk), .Q(register_26_q));  // open: clr
  Register #(.width(32)) register_27 (.D(wdata), .en(decoder_1_out21), .clk(clk), .Q(register_27_q));  // open: clr
  Register #(.width(32)) register_28 (.D(wdata), .en(decoder_1_out31), .clk(clk), .Q(register_28_q));  // open: clr
  Register #(.width(32)) register_29 (.D(wdata), .en(decoder_1_out7), .clk(clk), .Q(register_29_q));  // open: clr
  Register #(.width(32)) register_30 (.D(wdata), .en(decoder_1_out15), .clk(clk), .Q(register_30_q));  // open: clr
  Register #(.width(32)) register_31 (.D(wdata), .en(decoder_1_out22), .clk(clk), .Q(register_31_q));  // open: clr
  Register #(.width(32)) register_32 (.D(wdata), .en(decoder_1_out23), .clk(clk), .Q(register_32_q));  // open: clr
  Multiplexer #(.select(5), .width(32)) multiplexer_1 (
    .in0({32{1'b0}}), .in1(register_5_q), .in2(register_9_q), .in3(register_13_q), .in4(register_17_q),
    .in5(register_21_q), .in6(register_25_q), .in7(register_29_q), .in8(register_3_q), .in9(register_6_q),
    .in10(register_10_q), .in11(register_14_q), .in12(register_18_q), .in13(register_22_q),
    .in14(register_26_q), .in15(register_30_q), .in16(register_7_q), .in17(register_11_q),
    .in18(register_15_q), .in19(register_19_q), .in20(register_23_q), .in21(register_27_q),
    .in22(register_31_q), .in23(register_32_q), .in24(register_1_q), .in25(register_4_q),
    .in26(register_8_q), .in27(register_12_q), .in28(register_16_q), .in29(register_20_q),
    .in30(register_24_q), .in31(register_28_q), .out(RD1), .sel(RDS1));
  Multiplexer #(.select(5), .width(32)) multiplexer_2 (
    .in0({32{1'b0}}), .in1(register_5_q), .in2(register_9_q), .in3(register_13_q), .in4(register_17_q),
    .in5(register_21_q), .in6(register_25_q), .in7(register_29_q), .in8(register_3_q), .in9(register_6_q),
    .in10(register_10_q), .in11(register_14_q), .in12(register_18_q), .in13(register_22_q),
    .in14(register_26_q), .in15(register_30_q), .in16(register_7_q), .in17(register_11_q),
    .in18(register_15_q), .in19(register_19_q), .in20(register_23_q), .in21(register_27_q),
    .in22(register_31_q), .in23(register_32_q), .in24(register_1_q), .in25(register_4_q),
    .in26(register_8_q), .in27(register_12_q), .in28(register_16_q), .in29(register_20_q),
    .in30(register_24_q), .in31(register_28_q), .out(RD2), .sel(RDS2));
endmodule

module minirv (
  input  addi,
  input  add,
  input  jalr,
  input  lui,
  input  lwlbu,
  input  in_6,
  input  in_7
);

  wire and_1_out, clock_1_out, clock_2_out, clock_3_out, comparator_1_eq, comparator_2_eq, comparator_3_eq,
       comparator_4_eq, comparator_5_eq, comparator_7_eq, comparator_7_gt, comparator_8_lt, is_sws, ju1, ju2,
       multiplexer_1_out, not_1_out, or_1_out, rgb_video_1_p1, rgb_video_1_p2, swsb_1_out_4, swsb_1_out_5,
       swsb_1_out_6, swsb_1_out_7, WE;
  wire [2:0] judge;
  wire [4:0] multiplexer_2_out;
  wire [7:0] multiplexer_9_out;
  wire [11:0] liji;
  wire [13:0] register_1_q_2;
  wire [24:0] rom_1_data;
  wire [31:0] adder_1_out, adder_4_out, bit_extender_1_out, bit_extender_2_out, demultiplexer_1_out0, lub,
       lw, multiplexer_3_out, multiplexer_4_out, multiplexer_6_out, multiplexer_7_out, multiplexer_8_out,
       ram_1_dout, RD, RD1, RD2, RD10, RD11, register_1_q;

  ROM #(.addrWidth(14), .dataWidth(32)) rom_1 (
    .addr(register_1_q_2), .data({liji[11:5], rom_1_data[24:12], liji[4:0], rom_1_data[6:0]}));
  Comparator #(.width(7)) comparator_1 (.a(rom_1_data[6:0]), .b(7'b0010011), .eq(comparator_1_eq));  // open: gt, lt
  Comparator #(.width(7)) comparator_2 (.a(rom_1_data[6:0]), .b(7'b0110011), .eq(comparator_2_eq));  // open: gt, lt
  Comparator #(.width(7)) comparator_3 (.a(rom_1_data[6:0]), .b(7'b1100111), .eq(comparator_3_eq));  // open: gt, lt
  Comparator #(.width(7)) comparator_4 (.a(rom_1_data[6:0]), .b(7'b0110111), .eq(comparator_4_eq));  // open: gt, lt
  Comparator #(.width(7)) comparator_5 (.a(rom_1_data[6:0]), .b(7'b0000011), .eq(comparator_5_eq));  // open: gt, lt
  Comparator #(.width(7)) comparator_6 (.a(rom_1_data[6:0]), .b(7'b0100011), .eq(ju2));  // open: gt, lt
  assign bit_extender_1_out = {{20{liji[11]}}, {liji[11:5], rom_1_data[24:20]}};  // Bit_Extender bit_extender_1
  Multiplexer #(.select(3)) multiplexer_1 (
    .in0(1'b1), .in1(1'b1), .in2(1'b1), .in3(1'b1), .in4(1'b1), .in5(1'b1), .in6(1'b0), .in7(1'b0),
    .out(multiplexer_1_out), .sel(judge));
  Clock clock_1 (.out(clock_1_out));
  and u_lw (ju1, comparator_5_eq, rom_1_data[13]);
  and sw (is_sws, ju2, rom_1_data[13]);
  Multiplexer #(.select(3), .width(5)) multiplexer_2 (
    .in1(rom_1_data[24:20]), .in6(rom_1_data[24:20]), .in7(rom_1_data[24:20]), .out(multiplexer_2_out),
    .sel(judge));  // open: in0, in2, in3, in4, in5
  Register #(.width(32)) register_1 (
    .D(multiplexer_4_out), .en(1'b1), .clk(clock_1_out),
    .Q({register_1_q[31:16], register_1_q_2, register_1_q[1:0]}), .clr(in_7));
  Clock clock_2 (.out(clock_2_out));
  Multiplexer #(.select(3), .width(32)) multiplexer_3 (
    .in0(RD10), .in1(adder_4_out), .in2(adder_1_out), .in3({liji[11:5], rom_1_data[24:12], {12{1'b0}}}),
    .in4(lub), .in5(lw), .out(multiplexer_3_out), .sel(judge));  // open: in6, in7
  Priority_Encoder priority_encoder_1 (
    .in0(comparator_1_eq), .in1(comparator_2_eq), .in2(comparator_3_eq), .in3(comparator_4_eq),
    .in4(comparator_5_eq), .in5(ju1), .in6(ju2), .in7(is_sws), .out(judge));  // open: en_in, gs, en_out
  assign bit_extender_2_out = {{20{liji[11]}}, liji};  // Bit_Extender bit_extender_2
  Multiplexer #(.select(3), .width(32)) multiplexer_4 (
    .in0(adder_1_out), .in1(adder_1_out), .in2(multiplexer_7_out), .in3(adder_1_out), .in4(adder_1_out),
    .in5(adder_1_out), .in6(adder_1_out), .in7(adder_1_out), .out(multiplexer_4_out), .sel(judge));
  Adder #(.width(32)) adder_1 (
    .a({register_1_q[31:16], register_1_q_2, register_1_q[1:0]}), .b(32'h4), .out(adder_1_out));  // open: cin, cout
  Adder #(.width(32)) adder_2 (.a(RD1), .b(bit_extender_2_out), .out(RD11));  // open: cin, cout
  GPR gpr_1 (
    .clk(clock_2_out), .wdata(multiplexer_3_out), .CH(liji[4:0]), .EN(multiplexer_1_out),
    .RDS1(rom_1_data[19:15]), .RDS2(multiplexer_2_out), .RD1(RD1), .RD2(RD2));
  Multiplexer #(.width(32)) multiplexer_5 (
    .in0({RD2[7:0], RD2[7:0], RD2[7:0], RD2[7:0]}), .in1(RD2), .out(RD), .sel(is_sws));
  Multiplexer #(.select(3), .width(32)) multiplexer_6 (
    .in4(RD10), .in5(RD10), .in6(RD11), .in7(RD11), .out(multiplexer_6_out), .sel(judge));  // open: in0, in1, in2, in3
  Adder #(.width(32)) adder_3 (.a(bit_extender_1_out), .b(RD1), .out(RD10));  // open: cin, cout
  Adder #(.width(32)) adder_4 (.a(RD1), .b(RD2), .out(adder_4_out));  // open: cin, cout
  Multiplexer #(.select(3), .width(32)) multiplexer_7 (
    .in2(RD10), .out(multiplexer_7_out), .sel(judge));  // open: in0, in1, in3, in4, in5, in6, in7
  swsb swsb_1 (
    .is_sw(is_sws), .a01(multiplexer_6_out[1:0]), .ju2(ju2), .out_4(swsb_1_out_4), .out_5(swsb_1_out_5),
    .out_6(swsb_1_out_6), .out_7(swsb_1_out_7));
  RAM #(.addrWidth(20), .asyncread("true"), .byteenables("byteEnables"), .dataWidth(32), .\type ("nonvolatile")) ram_1 (
    .addr(multiplexer_6_out[21:2]), .we(WE), .oe(1'b1), .clk(clock_3_out), .din(RD), .dout(ram_1_dout),
    .be3(swsb_1_out_7), .be2(swsb_1_out_6), .be1(swsb_1_out_5), .be0(swsb_1_out_4));
  Clock clock_3 (.out(clock_3_out));
  Demultiplexer #(.width(32)) demultiplexer_1 (.out0(demultiplexer_1_out0), .out1(lw), .in(ram_1_dout), .sel(ju1));
  Multiplexer #(.select(3), .width(32)) multiplexer_8 (
    .in0(RD10), .in1(RD10), .in2(RD10), .in3(RD10), .in4(RD10), .in5(RD10), .in6(RD11), .in7(RD11),
    .out(multiplexer_8_out), .sel(judge));
  Multiplexer #(.select(2), .width(8)) multiplexer_9 (
    .in0(demultiplexer_1_out0[7:0]), .in1(demultiplexer_1_out0[15:8]), .in2(demultiplexer_1_out0[23:16]),
    .in3(demultiplexer_1_out0[31:24]), .out(multiplexer_9_out), .sel(multiplexer_6_out[1:0]));
  assign lub = {{24{multiplexer_9_out[7]}}, multiplexer_9_out};  // Bit_Extender bit_extender_3
  Comparator #(.width(32)) comparator_7 (
    .a(multiplexer_8_out), .b(32'h20000000), .gt(comparator_7_gt), .eq(comparator_7_eq));  // open: lt
  Comparator #(.width(32)) comparator_8 (
    .a(multiplexer_8_out), .b(32'h20040000), .lt(comparator_8_lt));  // open: gt, eq
  or or_1 (or_1_out, comparator_7_gt, comparator_7_eq);
  and and_1 (and_1_out, or_1_out, comparator_8_lt);
  // RGB_Video #(.cursor("No Cursor"), .height(256), .width(256)) rgb_video_1: pin names not known; wires that end beside it: rgb_video_1_p1, rgb_video_1_p2, multiplexer_8_out[9:2], multiplexer_8_out[17:10], RD2[23:0]
  Clock clock_4 (.out(rgb_video_1_p1));
  and and_2 (rgb_video_1_p2, and_1_out, ju2);
  not not_1 (not_1_out, and_1_out);
  and and_3 (WE, not_1_out, ju2);

  // Notes on the sheet:
  //   contents of rom_1 (hex, n*v repeats v):
  //   413 93137 10113 10b7 dbc08093 80e7 fe012823 fea10923 fea12423 fe914203 fe4109a3 ff012783 f787b3
  //   f787b3 4b6b7 f0068693 fdc10113 d787b3 10000713 f12423 10593 100793 b00513 2112023 12023 12223 e12623
  //   e12823 f10a23 10b7 a8408093 80e7 2012083 2410113 8067 ff410113 112423 10b7 a7c08093 80e7 513 1800093
  //   80e7 812083 513 c10113 8067 852583 feb12823 fe812e23 3437 a0840413 ff014183 3401b3 1c183 ff114203
  //   440233 24203 4181b3 ff214203 440233 24203 4181b3 ff314203 440233 24203 4181b3 3237 a0020213 320233
  //   24203 ffc12403 420233 420233 410233 11b7 85c18193 fe312823 14800193 fe312623 fec22203 20067 1052703
  //   52683 452783 fe810113 e12423 112a23 fed12823 fef12623 13737 c0070713 fe012223 ff314203 fe4102a3
  //   fef14203 fe410223 fe412203 470233 24203 fe4105a3 ff214203 fe4102a3 fee14203 fe410223 fe412203 470233
  //   24203 fe410523 ff114203 fe4102a3 fed14203 fe410223 fe412203 470233 24203 fe4104a3 ff014203 fe4102a3
  //   fec14203 fe410223 fe412203 470233 24203 fe410423 fe812703 c52603 fee12823 fe812e23 3437 a0840413
  //   ff014183 3401b3 1c183 ff114203 440233 24203 4181b3 ff214203 440233 24203 4181b3 ff314203 440233
  //   24203 4181b3 3237 a0020213 320233 24203 ffc12403 420233 420233 410233 66800193 fe312823 28000193
  //   fe312623 fec22203 20067 c68733 10000513 fe812e23 fe912c23 fee12823 50413 ff012483 fe812423 feb14183
  //   3181b3 fe312423 fe914183 3181b3 fe912423 feb14203 420233 fe412423 fe914203 4181b3 3181b3 fe312a23
  //   fe912423 33237 b0020213 feb14183 4181b3 1c183 fe3103a3 fea14183 4181b3 1c183 fe310323 fe914183
  //   4181b3 1c183 fe3102a3 fe814183 4181b3 1c183 fe310223 ff412183 fe412203 440233 120213 fe412423
  //   feb14203 420233 fe412423 fe914203 4181b3 3237 b0820213 320233 ff812483 ffc12403 24203 420233 420233
  //   410233 11b7 86018193 fe312823 38800193 fe312623 fec22203 20067 812703 10000513 812823 e78733
  //   fe812e23 fe912c23 fee12823 50413 ff012483 fe812423 feb14183 3181b3 fe312423 fe914183 3181b3 fe912423
  //   feb14203 420233 fe412423 fe914203 4181b3 3181b3 fe312a23 fe912423 33237 b0020213 feb14183 4181b3
  //   1c183 fe3103a3 fea14183 4181b3 1c183 fe310323 fe914183 4181b3 1c183 fe3102a3 fe814183 4181b3 1c183
  //   fe310223 ff412183 fe412203 440233 120213 fe412423 feb14203 420233 fe412423 fe914203 4181b3 3237
  //   b0820213 320233 ff812483 ffc12403 24203 420233 420233 410233 11b7 86418193 fe312823 49800193
  //   fe312623 fec22203 20067 8*f787b3 d787b3 f787b3 f787b3 20000437 f40433 812783 c60633 c60633 fef12423
  //   feb14183 3181b3 fe312423 fe914183 fff78213 fe412423 feb14203 420233 fe412423 fe914203 4181b3 3237
  //   b1820213 418233 24203 420233 420233 410233 65800193 fe312823 53c00193 fe312623 fec22203 20067 912623
  //   493 40513 c12223 b12023 10b7 de008093 80e7 12583 412603 812783 148493 40040413 c585b3 fef12823
  //   fe912623 fe812e23 fe912c23 4b437 d0040413 ff014183 340233 100193 320023 fec14183 3401b3 18023 24183
  //   ff114483 940233 100493 920023 fed14483 9404b3 48023 24483 9181b3 ff214483 940233 100493 920023
  //   fee14483 9404b3 48023 24483 9181b3 ff314483 940233 100493 920023 fef14483 9404b3 48023 24483 9181b3
  //   3237 a0020213 320233 24203 ff812483 ffc12403 420233 420233 410233 65400193 fe312823 54400193
  //   fe312623 fec22203 20067 c12483 1012403 1412083 1810113 8067 10000713 fec12823 fee12623 fe812e23
  //   fe912c23 4b437 d0040413 ff014183 340233 100193 320023 fec14183 3401b3 18023 24183 ff114483 940233
  //   100493 920023 fed14483 9404b3 48023 24483 9181b3 ff214483 940233 100493 920023 fee14483 9404b3 48023
  //   24483 9181b3 ff314483 940233 100493 920023 fef14483 9404b3 48023 24483 9181b3 3237 a0020213 320233
  //   24203 ff812483 ffc12403 420233 420233 410233 74c00193 fe312823 28000193 fe312623 fec22203 20067
  //   812703 fee12823 fec12623 fe812e23 fe912c23 4b437 d0040413 ff014183 340233 100193 320023 fec14183
  //   3401b3 18023 24183 ff114483 940233 100493 920023 fed14483 9404b3 48023 24483 9181b3 ff214483 940233
  //   100493 920023 fee14483 9404b3 48023 24483 9181b3 ff314483 940233 100493 920023 fef14483 9404b3 48023
  //   24483 9181b3 3237 a0020213 320233 24203 ff812483 ffc12403 420233 420233 410233 11b7 83418193
  //   fe312823 38800193 fe312623 fec22203 20067 1412083 40637 20000537 1810113 1237 de020213 20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
endmodule

module swsb (
  input  is_sw,
  input  [1:0] a01,
  input  ju2,
  output out_4,
  output out_5,
  output out_6,
  output out_7
);

  wire demultiplexer_1_out0, demultiplexer_1_out1, demultiplexer_1_out2, demultiplexer_1_out3;

  or or_1 (out_4, demultiplexer_1_out0, is_sw);
  or or_2 (out_5, demultiplexer_1_out1, is_sw);
  or or_3 (out_6, demultiplexer_1_out2, is_sw);
  or or_4 (out_7, demultiplexer_1_out3, is_sw);
  Demultiplexer #(.enable("true"), .select(2)) demultiplexer_1 (
    .out0(demultiplexer_1_out0), .out1(demultiplexer_1_out1), .out2(demultiplexer_1_out2),
    .out3(demultiplexer_1_out3), .in(1'b1), .sel(a01), .en(ju2));
endmodule
